// Digital circuit ADD.dig as structural Verilog
module ADD (
  input  [15:0] a,
  input  [15:0] b,
  output [19:0] out
);

  wire and_1_out, and_2_out, not_1_out, not_2_out, not_3_out;

  Add #(.Bits(16)) add_1 (.a(a), .b(b), .c_i(1'b0), .s({out[18], out[14:0]}), .c_o(out[17]));
  not not_1 (not_1_out, a[15]);
  not not_2 (not_2_out, b[15]);
  not not_3 (not_3_out, out[18]);
  Comparator #(.Bits(16)) comparator_1 (.a({16{1'b0}}), .b({out[18], out[14:0]}), .eq(out[19]));  // open: gt, lt
  and and_1 (and_1_out, out[18], not_1_out, not_2_out);
  and and_2 (and_2_out, not_3_out, b[15], a[15]);
  or or_1 (out[16], and_1_out, and_2_out);

  assign out[15] = out[18];
endmodule
