// Digital circuit AND.dig as structural Verilog
module AND (
  input  [15:0] a,
  input  [15:0] b,
  output [19:0] out
);

  assign {out[18], out[14:0]} = a & b;  // And and_1, 16 bits wide
  Comparator #(.Bits(16)) comparator_1 (.a({16{1'b0}}), .b({out[18], out[14:0]}), .eq(out[19]));  // open: gt, lt

  assign out[17:15] = {2'b00, out[18]};
endmodule
