// Digital circuit ArithmeticLogicUnit.dig as structural Verilog
module ArithmeticLogicUnit (
  input  [15:0] A,
  input  [15:0] B,
  input  [4:0] CTRL,
  input  CLK,
  output [15:0] R,
  output [3:0] F
);

  wire [19:0] add_1_out, and_1_out, cmp_1_out, dec_1_out, div_1_out, inc_1_out, logicshiftleft_lsl_1_out,
       logicshiftright_lsr_1_out, mod_1_p1, mul_1_out, not_1_out, or_1_out, rotateshiftleft_rsl_1_out,
       rotateshiftright_rsr_1_out, sub_1_out, through_1_out, through_2_out, through_3_out, xor_1_out;

  THROUGH through_1 (.a(B), .out(through_1_out));
  THROUGH through_2 (.a(B), .out(through_2_out));
  ADD add_1 (.a(A), .b(B), .out(add_1_out));
  SUB sub_1 (.a(A), .b(B), .out(sub_1_out));
  LogicShiftLeft_LSL logicshiftleft_lsl_1 (.CLK(CLK), .A(A), .B(B), .out(logicshiftleft_lsl_1_out));
  LogicShiftRight_LSR logicshiftright_lsr_1 (.CLK(CLK), .A(A), .B(B), .out(logicshiftright_lsr_1_out));
  RotateShiftLeft_RSL rotateshiftleft_rsl_1 (.CLK(CLK), .A(A), .B(B), .out(rotateshiftleft_rsl_1_out));
  RotateShiftRight_RSR rotateshiftright_rsr_1 (.CLK(CLK), .A(A), .B(B), .out(rotateshiftright_rsr_1_out));
  MUL mul_1 (.a(A), .b(B), .out(mul_1_out));
  DIV div_1 (.a(A), .b(B), .out(div_1_out));
  // MOD mod_1: pin names not known; wires that end beside it: mod_1_p1
  AND and_1 (.a(A), .b(B), .out(and_1_out));
  OR or_1 (.a(A), .b(B), .out(or_1_out));
  XOR xor_1 (.a(A), .b(B), .out(xor_1_out));
  NOT not_1 (.a(A), .out(not_1_out));
  CMP cmp_1 (.a(A), .b(B), .out(cmp_1_out));
  INC inc_1 (.a(A), .out(inc_1_out));
  DEC dec_1 (.a(A), .out(dec_1_out));
  THROUGH through_3 (.a(B), .out(through_3_out));
  Multiplexer #(.Selector_Bits(5), .Bits(20)) multiplexer_1 (
    .sel(CTRL), .in_0({20{1'b0}}), .in_1(through_1_out), .in_2(through_2_out), .in_3(add_1_out),
    .in_4(sub_1_out), .in_5(logicshiftleft_lsl_1_out), .in_6(logicshiftright_lsr_1_out),
    .in_7(rotateshiftleft_rsl_1_out), .in_8(rotateshiftright_rsr_1_out), .in_9(through_3_out),
    .in_10(mul_1_out), .in_11(div_1_out), .in_12(mod_1_p1), .in_13(and_1_out), .in_14(or_1_out),
    .in_15(xor_1_out), .in_16(not_1_out), .in_17(cmp_1_out), .in_18(inc_1_out), .in_19(dec_1_out),
    .in_20({20{1'b0}}), .in_21({20{1'b0}}), .in_22({20{1'b0}}), .in_23({20{1'b0}}), .in_24({20{1'b0}}),
    .in_25({20{1'b0}}), .in_26({20{1'b0}}), .in_27({20{1'b0}}), .in_28({20{1'b0}}), .in_29({20{1'b0}}),
    .in_30({20{1'b0}}), .in_31({20{1'b0}}), .out({F, R}));
endmodule
