// Digital circuit CMP.dig as structural Verilog
module CMP (
  input  [15:0] a,
  input  [15:0] b,
  output [19:0] out
);

  Comparator #(.Bits(16)) comparator_1 (.a(a), .b(b), .eq(out[19]), .lt(out[18]));  // open: gt

  assign out[17:0] = {18{1'b0}};
endmodule
