// Digital circuit MUL.dig as structural Verilog
module MUL (
  input  [15:0] a,
  input  [15:0] b,
  output [19:0] out
);

  wire and_1_out, and_2_out, and_3_out, and_4_out, and_5_out, comparator_1_eq, comparator_2_eq, not_1_out,
       not_2_out, not_3_out, not_4_out, not_5_out, not_6_out, not_7_out, not_8_out;
  wire [31:16] mul_1_mul;

  Mul #(.Bits(16), .Signed("true")) mul_1 (.a(a), .b(b), .mul({mul_1_mul, out[18], out[14:0]}));
  Comparator #(.Bits(16)) comparator_1 (.a({16{1'b1}}), .b(mul_1_mul), .eq(comparator_1_eq));  // open: gt, lt
  Comparator #(.Bits(16)) comparator_2 (.a({16{1'b0}}), .b(mul_1_mul), .eq(comparator_2_eq));  // open: gt, lt
  not not_1 (not_1_out, comparator_1_eq);
  not not_2 (not_2_out, comparator_2_eq);
  and and_1 (and_1_out, not_3_out, not_4_out, out[18]);
  not not_3 (not_3_out, a[15]);
  not not_4 (not_4_out, b[15]);
  and and_2 (and_2_out, not_5_out, b[15], not_6_out);
  not not_5 (not_5_out, a[15]);
  not not_6 (not_6_out, out[18]);
  and and_3 (and_3_out, a[15], not_7_out, not_8_out);
  not not_7 (not_7_out, b[15]);
  not not_8 (not_8_out, out[18]);
  and and_4 (and_4_out, a[15], b[15], out[18]);
  and and_5 (and_5_out, not_1_out, not_2_out);
  Comparator #(.Bits(16)) comparator_3 (.a({16{1'b0}}), .b({out[18], out[14:0]}), .eq(out[19]));  // open: gt, lt
  or or_1 (out[16], and_1_out, and_2_out, and_5_out, and_3_out, and_4_out);

  assign {out[17], out[15]} = {1'b0, out[18]};
endmodule
