// Digital circuit RotateShiftRight(RSR).dig as structural Verilog
module RotateShiftRight_RSR (
  input  CLK,
  input  [15:0] A,
  input  [15:0] B,
  output [19:0] out
);

  wire comparator_1_eq, register_1_q;
  wire [15:0] dec_1_out, multiplexer_1_out, multiplexer_2_out, register_2_q, register_3_q;
  wire [19:16] dec_1_out_2;

  Multiplexer #(.Bits(16)) multiplexer_1 (.sel(register_1_q), .in_0(A), .in_1(register_2_q), .out(multiplexer_1_out));
  Multiplexer #(.Bits(16)) multiplexer_2 (.sel(register_1_q), .in_0(B), .in_1(dec_1_out), .out(multiplexer_2_out));
  Register register_1 (.D(CLK), .C(CLK), .en(1'b1), .Q(register_1_q));
  Register #(.Bits(16)) register_2 (
    .D(multiplexer_1_out), .C(CLK), .en(1'b1), .Q({register_2_q[14:0], register_2_q[15]}));
  Register #(.Bits(16)) register_3 (.D(multiplexer_2_out), .C(CLK), .en(1'b1), .Q(register_3_q));
  DEC dec_1 (.a(register_3_q), .out({dec_1_out_2, dec_1_out}));
  Comparator #(.Bits(16)) comparator_1 (.a({16{1'b0}}), .b(dec_1_out), .eq(comparator_1_eq));  // open: gt, lt
  assign {out[18], out[14:0]} = comparator_1_eq ? register_2_q : 16'bz;  // Driver driver_1
  Comparator #(.Bits(16)) comparator_2 (.a({16{1'b0}}), .b({out[18], out[14:0]}), .eq(out[19]));  // open: gt, lt
  assign out[16] = comparator_1_eq ? 1'b0 : 1'bz;  // Driver driver_2
  assign out[17] = comparator_1_eq ? 1'b0 : 1'bz;  // Driver driver_3

  assign out[15] = out[18];

  // Notes on the sheet:
  //   A: default 32776
  //   B: default 5
endmodule
