// Digital circuit SUB.dig as structural Verilog
module SUB (
  input  [15:0] a,
  input  [15:0] b,
  output [19:0] out
);

  wire xnor_1_out, xor_1_out;

  Sub #(.Bits(16)) sub_1 (.a(a), .b(b), .c_i(1'b0), .s({out[18], out[14:0]}), .c_o(out[17]));
  xor xor_1 (xor_1_out, b[15], a[15]);
  xnor xnor_1 (xnor_1_out, out[18], b[15]);
  Comparator #(.Bits(16)) comparator_1 (.a({16{1'b0}}), .b({out[18], out[14:0]}), .eq(out[19]));  // open: gt, lt
  and and_1 (out[16], xnor_1_out, xor_1_out);

  assign out[15] = out[18];
endmodule
