// Digital circuit ControlUnit.dig as structural Verilog
module ControlUnit (
  input  [3:0] Fl,
  input  [5:0] Op,
  input  [4:0] Fu,
  output Br,
  output We,
  output A,
  output Ld,
  output Str,
  output Jmp,
  output En,
  output [4:0] Ctrl,
  output push,
  output pop
);

  wire and_3_out, and_7_out, and_8_out, and_9_out, and_10_out, and_11_out, nor_1_out, not_1_out, not_2_out,
       not_3_out, not_4_out, not_5_out, not_6_out, not_7_out, not_8_out, not_9_out, not_10_out, not_11_out,
       not_12_out, not_13_out, not_14_out, not_15_out, not_16_out, not_17_out, not_18_out, not_19_out,
       not_20_out, not_21_out, not_22_out, not_23_out, not_24_out, not_25_out, not_26_out, not_27_out,
       not_28_out, not_29_out, not_30_out, not_31_out, not_32_out, not_33_out, not_34_out, not_35_out,
       not_36_out, not_37_out, not_38_out, not_39_out, not_40_out;

  not not_1 (not_1_out, Op[4]);
  not not_2 (not_2_out, Op[3]);
  not not_3 (not_3_out, Op[0]);
  not not_4 (not_4_out, Op[4]);
  not not_5 (not_5_out, Op[3]);
  not not_6 (not_6_out, Op[5]);
  not not_7 (not_7_out, Op[4]);
  not not_8 (not_8_out, Op[2]);
  not not_9 (not_9_out, Op[1]);
  not not_10 (not_10_out, Fu[4]);
  not not_11 (not_11_out, Fu[2]);
  not not_12 (not_12_out, Fu[1]);
  not not_13 (not_13_out, Op[5]);
  not not_14 (not_14_out, Op[4]);
  not not_15 (not_15_out, Op[3]);
  not not_16 (not_16_out, Op[2]);
  not not_17 (not_17_out, Op[1]);
  not not_18 (not_18_out, Op[5]);
  not not_19 (not_19_out, Op[4]);
  not not_20 (not_20_out, Op[3]);
  not not_21 (not_21_out, Op[2]);
  not not_22 (not_22_out, Op[0]);
  not not_23 (not_23_out, Op[4]);
  not not_24 (not_24_out, Op[3]);
  not not_25 (not_25_out, Op[2]);
  not not_26 (not_26_out, Op[1]);
  not not_27 (not_27_out, Op[4]);
  not not_28 (not_28_out, Op[3]);
  not not_29 (not_29_out, Op[2]);
  not not_30 (not_30_out, Op[0]);
  not not_31 (not_31_out, Op[4]);
  not not_32 (not_32_out, Op[3]);
  not not_33 (not_33_out, Op[2]);
  not not_34 (not_34_out, Op[4]);
  not not_35 (not_35_out, Op[3]);
  not not_36 (not_36_out, Op[1]);
  not not_37 (not_37_out, Op[0]);
  not not_38 (not_38_out, Op[4]);
  not not_39 (not_39_out, Op[3]);
  not not_40 (not_40_out, Op[1]);
  nor nor_1 (nor_1_out, Op[0], Op[1], Op[2], Op[3], Op[4], Op[5]);
  and and_1 (push, Op[5], not_1_out, not_2_out, Op[2], Op[1], not_3_out);
  and and_2 (pop, Op[5], not_4_out, not_5_out, Op[2], Op[1], Op[0]);
  and and_3 (and_3_out, not_6_out, not_7_out, Op[3], not_8_out, not_9_out, Op[0]);
  and and_4 (A, nor_1_out, not_10_out, Fu[3], not_11_out, not_12_out, Fu[0]);
  and and_5 (Ld, not_13_out, not_14_out, not_15_out, not_16_out, not_17_out, Op[0]);
  and and_6 (Str, not_18_out, not_19_out, not_20_out, not_21_out, Op[1], not_22_out);
  Multiplexer #(.Bits(5)) multiplexer_1 (.sel(nor_1_out), .in_0(Op[4:0]), .in_1(Fu), .out(Ctrl));
  and and_7 (and_7_out, Op[5], not_23_out, not_24_out, not_25_out, not_26_out, Op[0], Fl[3]);
  and and_8 (and_8_out, Op[5], not_27_out, not_28_out, not_29_out, Op[1], not_30_out, Fl[2]);
  and and_9 (and_9_out, Op[5], not_31_out, not_32_out, not_33_out, Op[1], Op[0], Fl[1]);
  and and_10 (and_10_out, Op[5], not_34_out, not_35_out, Op[2], not_36_out, not_37_out, Fl[0]);
  and and_11 (and_11_out, Op[5], not_38_out, not_39_out, Op[2], not_40_out, Op[0]);
  or or_1 (En, push, pop);
  or or_2 (We, and_3_out, A, Ld);
  or or_3 (Br, and_7_out, and_8_out, and_9_out, and_10_out, and_11_out);

  assign Jmp = Op[5];
endmodule
