// Digital circuit FinalProcessor.dig as structural Verilog
module FinalProcessor (
  input  CLK,
  input  [15:0] Instruction,
  input  Load_Store
);

  wire controlunit_1_a, controlunit_1_br, controlunit_1_en, controlunit_1_jmp, controlunit_1_ld,
       controlunit_1_pop, controlunit_1_push, controlunit_1_str, controlunit_1_we, not_1_out, not_2_out;
  wire [3:0] arithmeticlogicunit_1_f, Flags_q;
  wire [4:0] controlunit_1_ctrl;
  wire [9:0] add_1_s, Instruction_Memory_d, multiplexer_1_out, multiplexer_2_out, PC_q, Stack_d;
  wire [15:0] Acc_q, arithmeticlogicunit_1_r, Data_Memory_d, demultiplexer_1_out_0, demultiplexer_1_out_1,
       multiplexer_3_out, multiplexer_4_out, multiplexer_5_out, Register_File_da, Sing_Extend_Unit_out, SP_q,
       sub_1_s;
  wire [15:10] Instruction_Memory_d_2;
  wire [19:0] dec_1_out, inc_1_out;

  Multiplexer #(.Bits(10)) multiplexer_1 (
    .sel(controlunit_1_jmp), .in_0(Stack_d), .in_1(add_1_s), .out(multiplexer_1_out));
  Multiplexer #(.Bits(10)) multiplexer_2 (
    .sel(controlunit_1_br), .in_0(Instruction_Memory_d), .in_1(multiplexer_1_out), .out(multiplexer_2_out));
  INC inc_1 (.a(SP_q), .out(inc_1_out));
  DEC dec_1 (.a(SP_q), .out(dec_1_out));
  Register #(.Bits(10)) PC (.D(multiplexer_2_out), .C(CLK), .en(1'b1), .Q(PC_q));
  Multiplexer #(.Bits(16)) multiplexer_3 (
    .sel(controlunit_1_push), .in_0(inc_1_out[15:0]), .in_1(dec_1_out[15:0]), .out(multiplexer_3_out));
  Add #(.Bits(10)) add_1 (.a(PC_q), .b(10'h1), .c_i(1'b0), .s(add_1_s));  // open: c_o
  RAMDualPort #(.AddrBits(10), .Bits(16)) Instruction_Memory (
    .A(PC_q), .Din(Instruction), .str(Load_Store), .C(CLK), .ld(not_1_out),
    .D({Instruction_Memory_d_2, Instruction_Memory_d}));
  not not_1 (not_1_out, Load_Store);
  Register #(.Bits(16)) SP (.D(multiplexer_3_out), .C(CLK), .en(controlunit_1_en), .Q(SP_q));
  Sub #(.Bits(16)) sub_1 (.a({16{1'b1}}), .b(SP_q), .c_i(1'b0), .s(sub_1_s));  // open: c_o
  ControlUnit controlunit_1 (
    .Fl(Flags_q), .Op(Instruction_Memory_d_2), .Fu(Instruction_Memory_d[4:0]), .Br(controlunit_1_br),
    .We(controlunit_1_we), .A(controlunit_1_a), .Ld(controlunit_1_ld), .Str(controlunit_1_str),
    .Jmp(controlunit_1_jmp), .En(controlunit_1_en), .Ctrl(controlunit_1_ctrl), .push(controlunit_1_push),
    .pop(controlunit_1_pop));
  BitExtender #(.inputBits(9)) Sing_Extend_Unit (.in(Instruction_Memory_d[8:0]), .out(Sing_Extend_Unit_out));
  RAMDualPort #(.AddrBits(16), .Bits(10)) Stack (
    .A(sub_1_s), .Din(PC_q), .str(controlunit_1_pop), .C(CLK), .ld(controlunit_1_push), .D(Stack_d));
  RegisterFile #(.AddrBits(1), .Bits(16)) Register_File (
    .Din(demultiplexer_1_out_1), .we(controlunit_1_we), .Rw(Instruction_Memory_d[9]), .C(CLK),
    .Ra(Instruction_Memory_d[9]), .Rb(1'b0), .Da(Register_File_da));  // open: Db
  not not_2 (not_2_out, controlunit_1_we);
  Register #(.Bits(16)) Acc (.D(demultiplexer_1_out_0), .C(CLK), .en(not_2_out), .Q(Acc_q));
  Demultiplexer #(.Bits(16)) demultiplexer_1 (
    .sel(controlunit_1_we), .in(multiplexer_5_out), .out_0(demultiplexer_1_out_0),
    .out_1(demultiplexer_1_out_1));
  Multiplexer #(.Bits(16)) multiplexer_4 (
    .sel(controlunit_1_a), .in_0(Sing_Extend_Unit_out), .in_1(Acc_q), .out(multiplexer_4_out));
  ArithmeticLogicUnit arithmeticlogicunit_1 (
    .A(Register_File_da), .B(multiplexer_4_out), .CTRL(controlunit_1_ctrl), .CLK(CLK),
    .R(arithmeticlogicunit_1_r), .F(arithmeticlogicunit_1_f));
  Register #(.Bits(4)) Flags (.D(arithmeticlogicunit_1_f), .C(CLK), .en(1'b1), .Q(Flags_q));
  EEPROMDualPort #(.AddrBits(16), .Bits(16)) Data_Memory (
    .A(arithmeticlogicunit_1_r), .Din(Register_File_da), .str(controlunit_1_str), .C(CLK),
    .ld(controlunit_1_ld), .D(Data_Memory_d));
  Multiplexer #(.Bits(16)) multiplexer_5 (
    .sel(controlunit_1_ld), .in_0(arithmeticlogicunit_1_r), .in_1(Data_Memory_d), .out(multiplexer_5_out));
endmodule
